// Logisim project μMIPS.circ as structural Verilog
module CPU (
  output I_Type_Ins,
  output R_Type_Ins
);

  wire and_1_p3, Clock, decoder_1_carry_out, decoder_1_led_enable, decoder_1_memwrite, decoder_1_pc_source,
       decoder_1_reg_w_e, decoder_1_zero_extend, LI, MemRead, nor_1_p1, nor_1_p2, nor_1_p3, not_1_p1,
       not_1_p2, not_2_out, not_3_out, not_4_p2;
  wire [2:0] field_split_1_rs, field_split_1_rt;
  wire [3:0] ALU_Op, led_display_1__1st_digit, led_display_1__2nd_digit, led_display_1__3rd_digit,
       led_display_1__4th_digit;
  wire [4:0] Opcode;
  wire [7:0] field_split_1_immediate, multiplexer_1_out, multiplexer_2_out, PC___1, PC_q;
  wire [15:0] ALU_A, ALU_B, bit_extender_1_out, bit_extender_2_out, bit_extender_3_out, imm, MemOut,
       multiplexer_3_out, multiplexer_4_out, r1_Data_In, rom_1_data, rt_out;
  wire [31:0] ALUResult;

  LED HALT (.in(not_1_p1));
  // NOT_Gate not_1: pin names not known; wires that end beside it: not_1_p1, not_1_p2
  Clock u_Clock (.out(Clock));
  Register PC (.D(multiplexer_2_out), .en(not_1_p2), .Q(PC_q), .clk(Clock));  // open: clr
  Multiplexer #(.width(8)) multiplexer_1 (
    .in0(field_split_1_immediate), .in1(ALU_A[7:0]), .out(multiplexer_1_out), .sel(decoder_1_pc_source));  // open: en
  Multiplexer #(.width(8)) multiplexer_2 (
    .in0(multiplexer_1_out), .in1(PC___1), .out(multiplexer_2_out), .sel(nor_1_p1));  // open: en
  Adder adder_1 (.a(PC_q), .b(8'h1), .out(PC___1));  // open: cin, cout
  Multiplexer #(.width(16)) multiplexer_3 (
    .in0(ALUResult[15:0]), .in1(MemOut), .out(multiplexer_3_out), .sel(MemRead));  // open: en
  // NOR_Gate nor_1: pin names not known; wires that end beside it: nor_1_p1, nor_1_p2, nor_1_p3
  ROM #(.dataWidth(16)) rom_1 (.addr(PC_q), .data(rom_1_data), .sel(1'b1));
  not not_2 (not_2_out, LI);
  Multiplexer #(.width(16)) multiplexer_4 (
    .in0(imm), .in1(multiplexer_3_out), .out(multiplexer_4_out), .sel(not_2_out));  // open: en
  assign bit_extender_1_out = {{8{1'b0}}, PC___1};  // Bit_Extender bit_extender_1
  Field_Split field_split_1 (
    .Instruction(rom_1_data), .OpCode(Opcode), .Rs(field_split_1_rs), .Immediate(field_split_1_immediate),
    .Rt(field_split_1_rt));
  Multiplexer #(.width(16)) multiplexer_5 (
    .in0(multiplexer_4_out), .in1(bit_extender_1_out), .out(r1_Data_In), .sel(nor_1_p3));  // open: en
  // AND_Gate and_1: pin names not known; wires that end beside it: nor_1_p2, ALUResult[0], and_1_p3
  Decoder decoder_1 (
    .Reg_W_E(decoder_1_reg_w_e), .ALU_Op(ALU_Op), .Jump(nor_1_p3), .Halt(not_1_p1), .Branch(and_1_p3),
    .Opcode(Opcode), .i_Type(I_Type_Ins), .LED_Enable(decoder_1_led_enable), .Carry_Out(decoder_1_carry_out),
    .MemWrite(decoder_1_memwrite), .MemRead(MemRead), .PC_Source(decoder_1_pc_source),
    .Zero_Extend(decoder_1_zero_extend), .LI(LI));
  Hex_Digit_Display hex_digit_display_1 (.value(led_display_1__4th_digit));  // open: dp
  assign bit_extender_2_out = {{8{1'b0}}, field_split_1_immediate};  // Bit_Extender bit_extender_2
  not not_3 (not_3_out, decoder_1_zero_extend);
  Multiplexer #(.width(16)) multiplexer_6 (
    .in0(bit_extender_2_out), .in1(bit_extender_3_out), .out(imm), .sel(not_3_out));  // open: en
  assign bit_extender_3_out = {{8{field_split_1_immediate[7]}}, field_split_1_immediate};  // Bit_Extender bit_extender_3
  Hex_Digit_Display hex_digit_display_2 (.value(led_display_1__2nd_digit));  // open: dp
  Hex_Digit_Display hex_digit_display_3 (.value(led_display_1__3rd_digit));  // open: dp
  LED_Display led_display_1 (
    ._4th_Digit(led_display_1__4th_digit), ._3rd_Digit(led_display_1__3rd_digit),
    ._2nd_Digit(led_display_1__2nd_digit), ._1st_Digit(led_display_1__1st_digit), .Input(ALU_A),
    .Clock(Clock), .Enable(decoder_1_led_enable));
  // NOT_Gate not_4: pin names not known; wires that end beside it: I_Type_Ins, not_4_p2
  Register_File register_file_1 (
    .Write_Data(r1_Data_In), .Overflow_Data(ALUResult[31:16]), .Write_Enable(decoder_1_reg_w_e),
    .Overflow_Enable(decoder_1_carry_out), .Write__r(field_split_1_rs), .Read__rs(field_split_1_rs),
    .Read__rt(field_split_1_rt), .Clock(Clock), .rs_Out(ALU_A), .rt_Out(rt_out));
  // Probe on rt_out
  Hex_Digit_Display hex_digit_display_4 (.value(led_display_1__1st_digit));  // open: dp
  Multiplexer #(.width(16)) multiplexer_7 (.in0(imm), .in1(rt_out), .out(ALU_B), .sel(not_4_p2));  // open: en
  RAM #(.dataWidth(16), .bus("separate")) ram_1 (
    .addr(rt_out[7:0]), .din(ALU_A), .data(MemOut), .str(decoder_1_memwrite), .clk(Clock), .ld(MemRead));  // open: sel, clr
  ALU alu_1 (
    .A_Input(ALU_A), .B_Input(ALU_B), .Op_Result(ALUResult[15:0]), .Result_Carry_Out(ALUResult[31:16]),
    .ALU_Op(ALU_Op));  // open: A_Invert, B_Invert
  // Probe on ALUResult
  // Probe on ALU_A
  // Probe on rt_out
  // Probe on imm
  // Probe on MemOut
  // Probe on r1_Data_In
  // Probe on ALUResult[31:16]
  // Probe on Opcode
  // Probe on ALU_Op
  // NOT_Gate not_5 has open pins: in=open, out=R_Type_Ins
  // Probe on ALU_A
  // Probe on ALU_B

  // Other names for the same wires on the sheet: rs_out[15:0] = ALU_A; r2_Data_In[15:0] = ALUResult[31:16];
  //   iType = I_Type_Ins

  // Notes on the sheet:
  //   StevenMontalbano
  //   smm285@pitt.edu
  //   Imm
  //   Progam Memory
  //   contents of rom_1 (hex, n*v repeats v):
  //   93fe 7200 8209 7200 a20c 6000 9414 7400 6000
  //   branch
  //   jump
  //   ALU Op
  //   Debug
endmodule

module Register_File (
  input  [15:0] Write_Data,
  input  [15:0] Overflow_Data,
  input  Write_Enable,
  input  Overflow_Enable,
  input  [2:0] Write__r,
  input  [2:0] Read__rs,
  input  [2:0] Read__rt,
  input  Clock,
  output [15:0] rs_Out,
  output [15:0] rt_Out
);

  wire or_1_out, or_2_out, or_3_out, or_4_out, or_5_out, or_6_out, or_7_out, or_8_out, r0, r0_2, r1, r1_2,
       r2, r2_2, r3, r3_2, r4, r4_2, r5, r5_2, r6, r6_2, r7, r7_2;
  wire [2:0] adder_1_out;
  wire [15:0] multiplexer_1_out, multiplexer_2_out, multiplexer_3_out, multiplexer_4_out, multiplexer_5_out,
       multiplexer_6_out, multiplexer_7_out, multiplexer_8_out, r0_q, r1_q, r2_q, r3_q, r4_q, r5_q, r6_q,
       r7_q;

  Adder #(.width(3)) adder_1 (.a(Write__r), .b(3'b001), .out(adder_1_out));  // open: cin, cout
  Demultiplexer #(.select(3)) demultiplexer_1 (
    .out0(r0), .out1(r1), .out2(r2), .out3(r3), .out4(r4), .out5(r5), .out6(r6), .out7(r7),
    .in(Write_Enable), .sel(Write__r));  // open: en
  Demultiplexer #(.select(3)) demultiplexer_2 (
    .out0(r0_2), .out1(r1_2), .out2(r2_2), .out3(r3_2), .out4(r4_2), .out5(r5_2), .out6(r6_2), .out7(r7_2),
    .in(Overflow_Enable), .sel(adder_1_out));  // open: en
  Multiplexer #(.width(16)) multiplexer_1 (
    .in0(Write_Data), .in1(Overflow_Data), .out(multiplexer_1_out), .sel(r0_2));  // open: en
  Multiplexer #(.width(16)) multiplexer_2 (
    .in0(Write_Data), .in1(Overflow_Data), .out(multiplexer_2_out), .sel(r1_2));  // open: en
  Multiplexer #(.width(16)) multiplexer_3 (
    .in0(Write_Data), .in1(Overflow_Data), .out(multiplexer_3_out), .sel(r2_2));  // open: en
  Multiplexer #(.width(16)) multiplexer_4 (
    .in0(Write_Data), .in1(Overflow_Data), .out(multiplexer_4_out), .sel(r3_2));  // open: en
  Multiplexer #(.width(16)) multiplexer_5 (
    .in0(Write_Data), .in1(Overflow_Data), .out(multiplexer_5_out), .sel(r4_2));  // open: en
  Multiplexer #(.width(16)) multiplexer_6 (
    .in0(Write_Data), .in1(Overflow_Data), .out(multiplexer_6_out), .sel(r5_2));  // open: en
  Multiplexer #(.width(16)) multiplexer_7 (
    .in0(Write_Data), .in1(Overflow_Data), .out(multiplexer_7_out), .sel(r6_2));  // open: en
  Multiplexer #(.width(16)) multiplexer_8 (
    .in0(Write_Data), .in1(Overflow_Data), .out(multiplexer_8_out), .sel(r7_2));  // open: en
  Register #(.width(16)) u_r0 (.D(multiplexer_1_out), .en(or_1_out), .Q(r0_q), .clk(Clock));  // open: clr
  or or_1 (or_1_out, r0, r0_2);
  Register #(.width(16)) u_r1 (.D(multiplexer_2_out), .en(or_2_out), .Q(r1_q), .clk(Clock));  // open: clr
  or or_2 (or_2_out, r1, r1_2);
  Register #(.width(16)) u_r2 (.D(multiplexer_3_out), .en(or_3_out), .Q(r2_q), .clk(Clock));  // open: clr
  or or_3 (or_3_out, r2, r2_2);
  Register #(.width(16)) u_r3 (.D(multiplexer_4_out), .en(or_4_out), .Q(r3_q), .clk(Clock));  // open: clr
  or or_4 (or_4_out, r3, r3_2);
  Register #(.width(16)) u_r4 (.D(multiplexer_5_out), .en(or_5_out), .Q(r4_q), .clk(Clock));  // open: clr
  or or_5 (or_5_out, r4, r4_2);
  Register #(.width(16)) u_r5 (.D(multiplexer_6_out), .en(or_6_out), .Q(r5_q), .clk(Clock));  // open: clr
  or or_6 (or_6_out, r5, r5_2);
  Register #(.width(16)) u_r6 (.D(multiplexer_7_out), .en(or_7_out), .Q(r6_q), .clk(Clock));  // open: clr
  or or_7 (or_7_out, r6, r6_2);
  Register #(.width(16)) u_r7 (.D(multiplexer_8_out), .en(or_8_out), .Q(r7_q), .clk(Clock));  // open: clr
  or or_8 (or_8_out, r7, r7_2);
  Multiplexer #(.select(3), .width(16)) multiplexer_9 (
    .in0(r0_q), .in1(r1_q), .in2(r2_q), .in3(r3_q), .in4(r4_q), .in5(r5_q), .in6(r6_q), .in7(r7_q),
    .out(rs_Out), .sel(Read__rs));  // open: en
  Multiplexer #(.select(3), .width(16)) multiplexer_10 (
    .in0(r0_q), .in1(r1_q), .in2(r2_q), .in3(r3_q), .in4(r4_q), .in5(r5_q), .in6(r6_q), .in7(r7_q),
    .out(rt_Out), .sel(Read__rt));  // open: en
  // Probe on r0_q
  // Probe on r1_q
  // Probe on r2_q
  // Probe on r3_q
  // Probe on r4_q
  // Probe on r5_q
  // Probe on r6_q
  // Probe on r7_q

  // Other names for the same wires on the sheet: Data_1[15:0] = Write_Data; Data_2[15:0] = Overflow_Data

  // Notes on the sheet:
  //   $r0
  //   $r1
  //   $r2
  //   $r3
  //   $r4
  //   $r5
  //   $r6
  //   $r7
endmodule

module ALU (
  input  [3:0] ALU_Op,
  input  [15:0] A_Input,
  input  [15:0] B_Input,
  input  A_Invert,
  input  B_Invert,
  output [15:0] Op_Result,
  output [15:0] Result_Carry_Out
);

  wire comparator_1_eq, comparator_1_gt, comparator_1_lt;
  wire [15:0] adder_1_out, and_1_out, bit_extender_1_out, bit_extender_3_out, divider_1_out, divider_1_rem,
       multiplexer_1_out, multiplexer_2_out, multiplier_1_cout, multiplier_1_out, nor_1_out, not_1_out,
       not_2_out, not_3_p1, not_3_p2, shifter_1_out, shifter_2_out, subtractor_1_out;

  // Probe on ALU_Op
  // Probe on A_Input
  // Probe on B_Input
  assign not_1_out = ~A_Input;  // NOT_Gate not_1, 16 bits wide
  assign not_2_out = ~B_Input;  // NOT_Gate not_2, 16 bits wide
  Multiplexer #(.width(16)) multiplexer_1 (
    .in0(A_Input), .in1(not_1_out), .out(multiplexer_1_out), .sel(A_Invert));  // open: en
  Multiplexer #(.width(16)) multiplexer_2 (
    .in0(B_Input), .in1(not_2_out), .out(multiplexer_2_out), .sel(B_Invert));  // open: en
  assign and_1_out = multiplexer_1_out & multiplexer_2_out;  // AND_Gate and_1, 16 bits wide
  assign nor_1_out = ~(multiplexer_1_out | multiplexer_2_out);  // NOR_Gate nor_1, 16 bits wide
  Adder #(.width(16)) adder_1 (.a(multiplexer_1_out), .b(multiplexer_2_out), .out(adder_1_out));  // open: cin, cout
  Subtractor #(.width(16)) subtractor_1 (
    .a(multiplexer_1_out), .b(multiplexer_2_out), .out(subtractor_1_out));  // open: bin, bout
  Multiplier #(.width(16)) multiplier_1 (
    .a(multiplexer_1_out), .b(multiplexer_2_out), .out(multiplier_1_out), .cout(multiplier_1_cout));  // open: cin
  Divider #(.width(16)) divider_1 (
    .a(multiplexer_1_out), .b(multiplexer_2_out), .out(divider_1_out), .rem(divider_1_rem));  // open: upper
  Shifter #(.width(16)) shifter_1 (.in(multiplexer_1_out), .\dist (multiplexer_2_out[3:0]), .out(shifter_1_out));
  Shifter #(.width(16), .shift("lr")) shifter_2 (
    .in(multiplexer_1_out), .\dist (multiplexer_2_out[3:0]), .out(shifter_2_out));
  Comparator #(.width(16)) comparator_1 (
    .a(multiplexer_1_out), .b({16{1'b0}}), .gt(comparator_1_gt), .eq(comparator_1_eq), .lt(comparator_1_lt));
  // NOT_Gate #(.width(16)) not_3: pin names not known; wires that end beside it: not_3_p1, not_3_p2
  assign bit_extender_1_out = {{15{1'b0}}, comparator_1_gt};  // Bit_Extender bit_extender_1
  assign not_3_p2 = {{15{1'b0}}, comparator_1_eq};  // Bit_Extender bit_extender_2
  assign bit_extender_3_out = {{15{1'b0}}, comparator_1_lt};  // Bit_Extender bit_extender_3
  Multiplexer #(.select(4), .width(16)) multiplexer_3 (
    .in0(and_1_out), .in1(nor_1_out), .in2(adder_1_out), .in3(subtractor_1_out), .in4(multiplier_1_out),
    .in5(divider_1_out), .in6(shifter_1_out), .in7(shifter_2_out), .in8(bit_extender_1_out), .in9(not_3_p2),
    .in10(not_3_p1), .in11(bit_extender_3_out), .in12({16{1'b0}}), .in13({16{1'b0}}), .in14({16{1'b0}}),
    .in15({16{1'b0}}), .out(Op_Result), .sel(ALU_Op));  // open: en
  Multiplexer #(.select(4), .width(16)) multiplexer_4 (
    .in0({16{1'b0}}), .in1({16{1'b0}}), .in2({16{1'b0}}), .in3({16{1'b0}}), .in4(multiplier_1_cout),
    .in5(divider_1_rem), .in6({16{1'b0}}), .in7({16{1'b0}}), .in8({16{1'b0}}), .in9({16{1'b0}}),
    .in10({16{1'b0}}), .in11({16{1'b0}}), .in12({16{1'b0}}), .in13({16{1'b0}}), .in14({16{1'b0}}),
    .in15({16{1'b0}}), .out(Result_Carry_Out), .sel(ALU_Op));  // open: en
endmodule

// Display
module LED_Display (
  input  [15:0] Input,
  input  Enable,
  input  Clock,
  output [3:0] _4th_Digit,
  output [3:0] _3rd_Digit,
  output [3:0] _2nd_Digit,
  output [3:0] _1st_Digit
);

  Register #(.width(16)) Hold_Value (
    .D(Input), .en(Enable), .Q({_4th_Digit, _3rd_Digit, _2nd_Digit, _1st_Digit}), .clk(Clock));  // open: clr
  Hex_Digit_Display hex_digit_display_1 (.value(_4th_Digit));  // open: dp
  Hex_Digit_Display hex_digit_display_2 (.value(_3rd_Digit));  // open: dp
  Hex_Digit_Display hex_digit_display_3 (.value(_2nd_Digit));  // open: dp
  // Probe on _2nd_Digit
  Hex_Digit_Display hex_digit_display_4 (.value(_1st_Digit));  // open: dp
  // Probe on _1st_Digit
endmodule

// Fields
module Field_Split (
  input  [15:0] Instruction,
  output [4:0] OpCode,
  output [2:0] Rs,
  output [7:0] Immediate,
  output [2:0] Rt
);


  assign Immediate = Instruction[8:1];
  assign OpCode = {Instruction[15:12], Instruction[0]};
  assign Rs = Instruction[11:9];
  assign Rt = Instruction[8:6];

  // Notes on the sheet:
  //   I Type: Opcode 15-12, 11-9 Rs, 8-1 Imm, 0 Supop 
  //   Opcode
  //   $Rs
  //   Imm
  //   $Rt
  //   R Type: Opcode 15-12, 11-9 Rs, 8-6 Rt, 5-1 NULL, 0 Supop 
endmodule

module Decoder (
  input  [4:0] Opcode,
  output Halt,
  output Reg_W_E,
  output LED_Enable,
  output MemWrite,
  output MemRead,
  output Carry_Out,
  output PC_Source,
  output LI,
  output Branch,
  output Jump,
  output [3:0] ALU_Op,
  output Zero_Extend,
  output i_Type
);

  wire add, addi, addui, \and , bn, bp, bx, bz, decoder_1_out10, decoder_1_out11, decoder_1_out12,
       decoder_1_out13, decoder_1_out14, decoder_1_out15, decoder_1_out18, decoder_1_out19, decoder_1_out24,
       decoder_1_out25, decoder_1_out26, decoder_1_out27, div, j_imm, jal, jr, mul, \nor , or_1_out,
       or_8_out, or_9_out, or_11_out, or_16_out, or_18_out, sllv, slrv, sub, undriven, undriven_2, undriven_3;

  Decoder_part #(.select(5)) decoder_1 (
    .out0(add), .out1(sub), .out2(\and ), .out3(\nor ), .out4(div), .out5(mul), .out6(slrv), .out7(sllv),
    .out8(MemRead), .out9(MemWrite), .out10(decoder_1_out10), .out11(decoder_1_out11),
    .out12(decoder_1_out12), .out13(decoder_1_out13), .out14(decoder_1_out14), .out15(decoder_1_out15),
    .out16(addui), .out17(addi), .out18(decoder_1_out18), .out19(decoder_1_out19), .out20(bp), .out21(bn),
    .out22(bx), .out23(bz), .out24(decoder_1_out24), .out25(decoder_1_out25), .out26(decoder_1_out26),
    .out27(decoder_1_out27), .sel(Opcode));  // open: out28, out29, out30, out31, en
  // Probe on Opcode
  or or_1 (or_1_out, add, addui, addi);
  Priority_Encoder #(.select(4)) priority_encoder_1 (
    .in0(1'b1), .in1(\nor ), .in2(or_1_out), .in3(sub), .in4(mul), .in5(div), .in6(sllv), .in7(slrv),
    .in8(bp), .in9(bz), .in10(bx), .in11(bn), .in12(1'b0), .in13(1'b0), .in14(1'b0), .in15(1'b0), .out(ALU_Op));  // open: gs, en_out, en_in
  or or_2 (jr, decoder_1_out10, decoder_1_out11, undriven);
  or or_3 (Halt, undriven, decoder_1_out12, decoder_1_out13);
  or or_4 (LED_Enable, decoder_1_out14, decoder_1_out15, undriven_2);
  or or_5 (LI, undriven_2, decoder_1_out18, decoder_1_out19);
  or or_6 (jal, decoder_1_out24, decoder_1_out25, undriven_3);
  or or_7 (j_imm, undriven_3, decoder_1_out26, decoder_1_out27);
  or or_8 (or_8_out, addui, jal, addi);
  or or_9 (or_9_out, add, sub, \and , \nor , div, mul);
  or or_10 (Reg_W_E, or_9_out, or_11_out);
  or or_11 (or_11_out, slrv, sllv, MemRead, LI, or_8_out);
  or or_12 (Carry_Out, div, mul);
  Priority_Encoder #(.select(1)) priority_encoder_2 (.in0(1'b1), .in1(jr), .out(PC_Source));  // open: gs, en_out, en_in
  or or_13 (Branch, bp, bn, bx, bz);
  or or_14 (Jump, jr, j_imm, jal);
  or or_15 (Zero_Extend, addui, LI);
  or or_16 (or_16_out, addi, j_imm, jal);
  or or_17 (i_Type, Zero_Extend, or_16_out, or_18_out);
  or or_18 (or_18_out, bp, bn, bx, bz);

  // Other names for the same wires on the sheet: lw = MemRead; put = LED_Enable; sw = MemWrite

  // Notes on the sheet:
  //   1 = Sign Extended (addi)
  //   0 default to Imm, 1 = $rs
endmodule
